// Logisim project 4-Bit Add-Sub.circ as structural Verilog: 1 circuit, main circuit main
module main (
  input  _1,
  input  _2,
  input  _4,
  input  _8,
  input  Cin,
  input  _1_2,
  input  _2_2,
  input  _4_2,
  input  _8_2,
  output _1_3,
  output _2_3,
  output _4_3,
  output _8_3,
  output _16
);

  wire main_1_p5, main_2_p5, main_3_p1, main_3_p6, main_4_p5, multiplexer_1_out, multiplexer_2_out,
       multiplexer_3_out, multiplexer_4_out, not_1_out, not_2_out, not_3_out, not_4_out, not_5_out;

  not not_1 (not_1_out, _1);
  Multiplexer multiplexer_1 (.in0(_1), .in1(not_1_out), .out(multiplexer_1_out), .sel(Cin));  // open: en
  // Full_Adder_main main_1: pin names not known; wires that end beside it: multiplexer_1_out, _1_2, Cin, _1_3, main_1_p5
  not not_2 (not_2_out, _2);
  Multiplexer multiplexer_2 (.in0(_2), .in1(not_2_out), .out(multiplexer_2_out), .sel(Cin));  // open: en
  // Full_Adder_main main_2: pin names not known; wires that end beside it: multiplexer_2_out, _2_2, main_1_p5, _2_3, main_2_p5
  not not_3 (not_3_out, _4);
  Multiplexer multiplexer_3 (.in0(_4), .in1(not_3_out), .out(multiplexer_3_out), .sel(Cin), .en(main_3_p1));
  not not_4 (not_4_out, _8);
  Multiplexer multiplexer_4 (.in0(_8), .in1(not_4_out), .out(multiplexer_4_out), .sel(Cin));  // open: en
  // Full_Adder_main main_3: pin names not known; wires that end beside it: main_3_p1, multiplexer_3_out, _4_2, main_2_p5, _4_3, main_3_p6
  // Full_Adder_main main_4: pin names not known; wires that end beside it: multiplexer_4_out, _8_2, main_3_p6, _8_3, main_4_p5
  not not_5 (not_5_out, Cin);
  and and_1 (_16, main_4_p5, not_5_out);
endmodule
