// Logisim project 4-Bit Adder.circ as structural Verilog: 1 circuit, main circuit main
module main (
  input  _1,
  input  _2,
  input  _4,
  input  _8,
  input  _1_2,
  input  _2_2,
  input  _4_2,
  input  _8_2,
  output _1_3,
  output _2_3,
  output _4_3,
  output _8_3,
  output _16
);

  wire main_1_p4, main_2_p5, main_3_p5;

  // Half_Adder_main main_1: pin names not known; wires that end beside it: _1, _1_2, _1_3, main_1_p4
  // Full_Adder_main main_2: pin names not known; wires that end beside it: _2, _2_2, main_1_p4, _2_3, main_2_p5
  // Full_Adder_main main_3: pin names not known; wires that end beside it: _4, _4_2, main_2_p5, _4_3, main_3_p5
  // Full_Adder_main main_4: pin names not known; wires that end beside it: _8, _8_2, main_3_p5, _8_3, _16
endmodule
