// Logisim project 4-Bit Multiplier.circ as structural Verilog: 1 circuit, main circuit main
module main (
  input  A8,
  input  A4,
  input  A2,
  input  A1,
  input  B8,
  input  B4,
  input  B2,
  input  B1,
  output P1,
  output P2,
  output P4,
  output P8,
  output P16,
  output P32,
  output P64,
  output P128
);

  wire and_1_out, and_2_out, and_3_out, and_5_out, and_6_out, and_7_out, and_8_out, and_9_out, and_10_out,
       and_11_out, and_12_out, and_13_out, and_14_out, and_15_out, and_16_out, main_1__2_3, main_1__4_3,
       main_1__8_3, main_1__16, main_2__2_3, main_2__4_3, main_2__8_3, main_2__16, not_1_out;

  not not_1 (not_1_out, 1'b1);
  and and_1 (and_1_out, B1, A8);
  and and_2 (and_2_out, A4, B1);
  and and_3 (and_3_out, A2, B1);
  and and_4 (P1, A1, B1);
  and and_5 (and_5_out, A8, B2);
  and and_6 (and_6_out, A4, B2);
  and and_7 (and_7_out, A2, B2);
  and and_8 (and_8_out, A1, B2);
  _4_Bit_Adder_main main_1 (
    ._1(and_3_out), ._2(and_2_out), ._4(and_1_out), ._8(not_1_out), ._1_2(and_8_out), ._2_2(and_7_out),
    ._4_2(and_6_out), ._8_2(and_5_out), ._1_3(P2), ._2_3(main_1__2_3), ._4_3(main_1__4_3),
    ._8_3(main_1__8_3), ._16(main_1__16));
  and and_9 (and_9_out, A8, B4);
  and and_10 (and_10_out, A4, B4);
  and and_11 (and_11_out, A2, B4);
  and and_12 (and_12_out, A1, B4);
  _4_Bit_Adder_main main_2 (
    ._1(main_1__2_3), ._2(main_1__4_3), ._4(main_1__8_3), ._8(main_1__16), ._1_2(and_12_out),
    ._2_2(and_11_out), ._4_2(and_10_out), ._8_2(and_9_out), ._1_3(P4), ._2_3(main_2__2_3),
    ._4_3(main_2__4_3), ._8_3(main_2__8_3), ._16(main_2__16));
  _4_Bit_Adder_main main_3 (
    ._1(main_2__2_3), ._2(main_2__4_3), ._4(main_2__8_3), ._8(main_2__16), ._1_2(and_16_out),
    ._2_2(and_15_out), ._4_2(and_14_out), ._8_2(and_13_out), ._1_3(P8), ._2_3(P16), ._4_3(P32), ._8_3(P64),
    ._16(P128));
  and and_13 (and_13_out, A8, B8);
  and and_14 (and_14_out, A4, B8);
  and and_15 (and_15_out, A2, B8);
  and and_16 (and_16_out, A1, B8);

  // Notes on the sheet:
  //   4-Bit +
  //   4-Bit +
  //   4-Bit +
endmodule
