// Logisim project 4-bit 2 input loader.circ as structural Verilog: 1 circuit, main circuit main
module main (
  input  I1,
  input  I2,
  input  I3,
  input  I4,
  input  Load,
  output A_In,
  output out_7,
  output out_8,
  output out_9,
  output B_In,
  output out_11,
  output out_12,
  output out_13
);

  wire and_1_out, and_2_out, t_ff_1_q, t_ff_1_qn, t_ff_2_q, t_ff_2_qn;

  T_Flip_Flop t_ff_1 (.clk(Load), .T(1'b1), .Q(t_ff_1_q), .Qn(t_ff_1_qn));  // open: preset, reset, en
  T_Flip_Flop t_ff_2 (.clk(Load), .T(t_ff_1_q), .Q(t_ff_2_q), .Qn(t_ff_2_qn));  // open: preset, reset, en
  and and_1 (and_1_out, t_ff_1_q, t_ff_2_qn);
  and and_2 (and_2_out, t_ff_1_qn, t_ff_2_q);
  // _4_bit_input_loader_main main_1: pin names not known; wires that end beside it: I1, I2, I3, I4, and_1_out, A_In, out_7, out_8, out_9
  // _4_bit_input_loader_main main_2: pin names not known; wires that end beside it: I1, I2, I3, I4, and_2_out, B_In, out_11, out_12, out_13

  // Notes on the sheet:
  //   A In
endmodule
