// Logisim project Calc w Input clicks.circ as structural Verilog: 1 circuit, main circuit main
module main (
  input  in_1,
  input  in_2,
  input  in_3,
  input  in_4,
  input  Mult_N_Y,
  input  in_6
);

  wire button_1_out, main_1_a_in, main_1_b_in, main_1_out_7, main_1_out_8, main_1_out_9, main_1_out_11,
       main_1_out_12, main_1_out_13, main_2_o1, main_2_o2, main_2_o4, main_2_o8, main_2_o16, main_2_o32,
       main_2_o64, main_2_o128;

  _4_bit_2_input_loader_main main_1 (
    .I1(in_1), .I2(in_2), .I3(in_3), .I4(in_4), .Load(button_1_out), .A_In(main_1_a_in),
    .out_7(main_1_out_7), .out_8(main_1_out_8), .out_9(main_1_out_9), .B_In(main_1_b_in),
    .out_11(main_1_out_11), .out_12(main_1_out_12), .out_13(main_1_out_13));
  Button button_1 (.out(button_1_out));
  Calculator_add_sub_mult_main main_2 (
    .A1(main_1_a_in), .A2(main_1_out_7), .A4(main_1_out_8), .A8(main_1_out_9), .B1(main_1_b_in),
    .B2(main_1_out_11), .B4(main_1_out_12), .B8(main_1_out_13), .Multiply_N_Y(Mult_N_Y), .in_10(in_6),
    .O1(main_2_o1), .O2(main_2_o2), .O4(main_2_o4), .O8(main_2_o8), .O16(main_2_o16), .O32(main_2_o32),
    .O64(main_2_o64), .O128(main_2_o128));
  LED led_1 (.in(main_2_o1));
  LED led_2 (.in(main_2_o2));
  LED led_3 (.in(main_2_o4));
  LED led_4 (.in(main_2_o8));
  LED led_5 (.in(main_2_o16));
  LED led_6 (.in(main_2_o32));
  LED led_7 (.in(main_2_o64));
  LED led_8 (.in(main_2_o128));

  // Notes on the sheet:
  //   Load
endmodule
