// Logisim project Calculator add-sub-mult.circ as structural Verilog: 1 circuit, main circuit main
module main (
  input  A1,
  input  A2,
  input  A4,
  input  A8,
  input  B1,
  input  B2,
  input  B4,
  input  B8,
  input  Multiply_N_Y,
  input  in_10,
  output O1,
  output O2,
  output O4,
  output O8,
  output O16,
  output O32,
  output O64,
  output O128
);

  wire main_1__02__mult, main_1_o1, main_2__02__mult, main_2_o1, main_3__02__mult, main_3_o1,
       main_4__02__mult, main_4_o1, main_5__02__mult, main_5_o1, main_6__02__mult, main_6_o1,
       main_7__02__mult, main_7_o1, main_8__02__mult, main_8_o1, main_9__1_3, main_9__2_3, main_9__4_3,
       main_9__8_3, main_9__16, main_10_p1, main_10_p2, main_10_p4, main_10_p8, main_10_p16;

  Path_Selector_main main_1 (.In(A1), .Switch(Multiply_N_Y), .O1(main_1_o1), ._02__Mult(main_1__02__mult));
  Path_Selector_main main_2 (.In(A2), .Switch(Multiply_N_Y), .O1(main_2_o1), ._02__Mult(main_2__02__mult));
  Path_Selector_main main_3 (.In(A4), .Switch(Multiply_N_Y), .O1(main_3_o1), ._02__Mult(main_3__02__mult));
  Path_Selector_main main_4 (.In(A8), .Switch(Multiply_N_Y), .O1(main_4_o1), ._02__Mult(main_4__02__mult));
  Path_Selector_main main_5 (.In(B1), .Switch(Multiply_N_Y), .O1(main_5_o1), ._02__Mult(main_5__02__mult));
  Path_Selector_main main_6 (.In(B2), .Switch(Multiply_N_Y), .O1(main_6_o1), ._02__Mult(main_6__02__mult));
  Path_Selector_main main_7 (.In(B4), .Switch(Multiply_N_Y), .O1(main_7_o1), ._02__Mult(main_7__02__mult));
  Path_Selector_main main_8 (.In(B8), .Switch(Multiply_N_Y), .O1(main_8_o1), ._02__Mult(main_8__02__mult));
  _4_Bit_Add_Sub_main main_9 (
    .Cin(in_10), ._1(main_1_o1), ._2(main_2_o1), ._4(main_3_o1), ._8(main_4_o1), ._1_2(main_5_o1),
    ._2_2(main_6_o1), ._4_2(main_7_o1), ._8_2(main_8_o1), ._1_3(main_9__1_3), ._2_3(main_9__2_3),
    ._4_3(main_9__4_3), ._8_3(main_9__8_3), ._16(main_9__16));
  _4_Bit_Multiplier_main main_10 (
    .A8(main_4__02__mult), .A4(main_3__02__mult), .A2(main_2__02__mult), .A1(main_1__02__mult),
    .B8(main_8__02__mult), .B4(main_7__02__mult), .B2(main_6__02__mult), .B1(main_5__02__mult),
    .P1(main_10_p1), .P2(main_10_p2), .P4(main_10_p4), .P8(main_10_p8), .P16(main_10_p16), .P32(O32),
    .P64(O64), .P128(O128));
  or or_1 (O1, main_9__1_3, main_10_p1);
  or or_2 (O8, main_10_p8, main_9__8_3);
  or or_3 (O2, main_10_p2, main_9__2_3);
  or or_4 (O4, main_9__4_3, main_10_p4);
  or or_5 (O16, main_9__16, main_10_p16);

  // Notes on the sheet:
  //   Note: switches use convention 0/1 -> N/Y, +/-
  //   Add-Sub
  //   Mult
endmodule
