// Logisim project Path Selector.circ as structural Verilog
module main (
  input  In,
  input  Switch,
  output O1,
  output _02__Mult
);

  wire not_1_out;

  not not_1 (not_1_out, Switch);
  and and_1 (O1, In, not_1_out);
  and and_2 (_02__Mult, In, Switch);
endmodule
